// Logisim project CPUdesign.circ as structural Verilog: 7 circuits, main circuit main
module main (
  input  rst
);

  wire clk_out, registerfile_1_p5, registerfile_1_p6;
  wire [3:0] alucontrol_1_op;
  wire [4:0] rA, rB, rW;
  wire [5:0] func;
  wire [15:6] imm;
  wire [31:0] adder_1_out, PC_q, ROM_data, shifter_1_out, undriven;
  wire [31:26] if_id_1_ir_2;

  Clock #(.highDuration(1), .lowDuration(1)) clk (.out(clk_out));
  Register #(.width(32), .trigger("rising"), .Select("low")) PC (
    .D(undriven), .Q(PC_q), .clk(clk_out), .clr(rst));  // open: en
  Shifter #(.width(32), .shift("ll")) shifter_1 (.in(PC_q), .\dist (5'b00010), .out(shifter_1_out));
  ROM #(.addrWidth(20), .dataWidth(32), .Select("low")) ROM (.addr(PC_q[19:0]), .data(ROM_data));
  Adder #(.width(32)) adder_1 (.a(32'h4), .b(shifter_1_out), .out(adder_1_out));  // open: cin, cout
  IF_ID if_id_1 (
    .PC_4(adder_1_out), .IR(ROM_data), .clr(rst), .IR_2({if_id_1_ir_2, rA, rB, imm, func}), .clk(clk_out));  // open: PC_4_2
  // RegisterFile registerfile_1: pin names not known; wires that end beside it: rW, rW, rA, rB, registerfile_1_p5, registerfile_1_p6, registerfile_1_p5, registerfile_1_p6
  ID_EX id_ex_1 ();  // open: PC_4, RegDst, Branch, MemRead, MemToReg, ALUOp, MemWrite, ALUSrc, RegWrite, clr, in_12, B, imm32, rt, rd, out_17, RegDst_2, Branch_2, MemRead_2, MemToReg_2, ALUOp_2, MemWrite_2, ALUSrc_2, RegWrite_2, out_26, out_27, out_28, out_29, out_30, in_10
  ALUcontrol alucontrol_1 (.Op(alucontrol_1_op));  // open: ALUOp, func
  ALU alu_1 (.op(alucontrol_1_op));  // open: A, B, Shamt, ALUresult, imm, ALUSrc

  // Other names for the same wires on the sheet: imm[5:0] = func; shamt[4:0] = imm[10:6]; rd[4:0] = imm[15:11];
  //   rt[4:0] = rB; rs[4:0] = rA
endmodule

module PC (
  input  [31:0] pcNew,
  input  clk,
  input  reset,
  output [31:0] pcOld
);

  Register #(.width(32), .trigger("rising"), .Select("low")) register_1 (
    .D(pcNew), .Q(pcOld), .clk(clk), .clr(reset));  // open: en
endmodule

module ALU (
  input  [31:0] A,
  input  [31:0] B,
  input  [15:0] imm,
  input  [4:0] Shamt,
  input  [1:0] ALUSrc,
  input  [3:0] op,
  output [31:0] ALUresult
);

  wire [31:0] adder_1_out, and_1_out, bit_extender_1_out, bit_extender_2_out, multiplexer_1_out,
       multiplier_1_out, or_1_out, shifter_1_out, shifter_2_out, shifter_3_out, xor_1_out;

  assign bit_extender_1_out = {{16{imm[15]}}, imm};  // Bit_Extender bit_extender_1
  assign bit_extender_2_out = {{16{1'b0}}, imm};  // Bit_Extender bit_extender_2
  Multiplexer #(.select(2), .width(32), .disabled("Z"), .enable("false")) multiplexer_1 (
    .in0(B), .in1(bit_extender_1_out), .in2(bit_extender_2_out), .in3({32{1'b0}}), .out(multiplexer_1_out),
    .sel(ALUSrc));
  // Probe on multiplexer_1_out
  assign and_1_out = A & multiplexer_1_out;  // AND_Gate and_1, 32 bits wide
  assign or_1_out = A | multiplexer_1_out;  // OR_Gate or_1, 32 bits wide
  assign xor_1_out = A ^ multiplexer_1_out;  // XOR_Gate xor_1, 32 bits wide
  Adder #(.width(32)) adder_1 (.a(A), .b(multiplexer_1_out), .out(adder_1_out));  // open: cin, cout
  Shifter #(.width(32), .shift("ll")) shifter_1 (.in(multiplexer_1_out), .\dist (Shamt), .out(shifter_1_out));
  Shifter #(.width(32), .shift("lr")) shifter_2 (.in(multiplexer_1_out), .\dist (Shamt), .out(shifter_2_out));
  Shifter #(.width(32), .shift("ll")) shifter_3 (.in(multiplexer_1_out), .\dist (5'b10000), .out(shifter_3_out));
  Multiplier #(.width(32)) multiplier_1 (.a(A), .b(multiplexer_1_out), .out(multiplier_1_out));  // open: cin, cout
  Multiplexer #(.select(4), .width(32), .disabled("Z"), .enable("false")) multiplexer_2 (
    .in0(and_1_out), .in1(or_1_out), .in2(xor_1_out), .in3(adder_1_out), .in4(shifter_1_out),
    .in5(shifter_2_out), .in6(shifter_3_out), .in7(multiplier_1_out), .out(ALUresult), .sel(op));  // open: in8, in9, in10, in11, in12, in13, in14, in15

  // Notes on the sheet:
  //   单元测试 
  //   lui
endmodule

module IF_ID (
  input  [31:0] PC_4,
  input  [31:0] IR,
  input  clr,
  input  clk,
  output [31:0] PC_4_2,
  output [31:0] IR_2
);

  wire \异步清零转同步清零_1_out_3 ;

  Register #(.width(32), .trigger("rising"), .Select("low")) register_1 (
    .D(PC_4), .Q(PC_4_2), .clk(clk), .clr(\异步清零转同步清零_1_out_3 ));  // open: en
  Register #(.width(32), .trigger("rising"), .Select("low")) register_2 (
    .D(IR), .Q(IR_2), .clk(clk), .clr(\异步清零转同步清零_1_out_3 ));  // open: en
  \异步清零转同步清零  \u_异步清零转同步清零_1  (.clk(clk), .clr(clr), .out_3(\异步清零转同步清零_1_out_3 ));

  // Notes on the sheet:
  //   上升沿清零，或者1的时候，或者下降沿也行，反正没有动作。
endmodule

module ID_EX (
  input  [31:0] PC_4,
  input  RegDst,
  input  Branch,
  input  MemRead,
  input  MemToReg,
  input  [1:0] ALUOp,
  input  MemWrite,
  input  ALUSrc,
  input  RegWrite,
  input  in_10,
  input  clr,
  input  [31:0] in_12,
  input  [31:0] B,
  input  [31:0] imm32,
  input  [4:0] rt,
  input  [4:0] rd,
  output [31:0] out_17,
  output RegDst_2,
  output Branch_2,
  output MemRead_2,
  output MemToReg_2,
  output [1:0] ALUOp_2,
  output MemWrite_2,
  output ALUSrc_2,
  output RegWrite_2,
  output [31:0] out_26,
  output [31:0] out_27,
  output [31:0] out_28,
  output [4:0] out_29,
  output [4:0] out_30
);

  wire \异步清零转同步清零_1_out_3 ;

  Register #(.width(32), .trigger("rising"), .Select("low")) u_PC_4 (
    .D(PC_4), .Q(out_17), .clk(in_10), .clr(\异步清零转同步清零_1_out_3 ));  // open: en
  Register #(.width(1), .trigger("rising"), .Select("low")) register_1 (
    .D(RegDst), .Q(RegDst_2), .clk(in_10), .clr(\异步清零转同步清零_1_out_3 ));  // open: en
  Register #(.width(1), .trigger("rising"), .Select("low")) register_2 (
    .D(Branch), .Q(Branch_2), .clk(in_10), .clr(\异步清零转同步清零_1_out_3 ));  // open: en
  Register #(.width(1), .trigger("rising"), .Select("low")) register_3 (
    .D(MemRead), .Q(MemRead_2), .clk(in_10), .clr(\异步清零转同步清零_1_out_3 ));  // open: en
  Register #(.width(1), .trigger("rising"), .Select("low")) register_4 (
    .D(MemToReg), .Q(MemToReg_2), .clk(in_10), .clr(\异步清零转同步清零_1_out_3 ));  // open: en
  Register #(.width(2), .trigger("rising"), .Select("low")) register_5 (
    .D(ALUOp), .Q(ALUOp_2), .clk(in_10), .clr(\异步清零转同步清零_1_out_3 ));  // open: en
  Register #(.width(1), .trigger("rising"), .Select("low")) register_6 (
    .D(MemWrite), .Q(MemWrite_2), .clk(in_10), .clr(\异步清零转同步清零_1_out_3 ));  // open: en
  Register #(.width(1), .trigger("rising"), .Select("low")) register_7 (
    .D(ALUSrc), .Q(ALUSrc_2), .clk(in_10), .clr(\异步清零转同步清零_1_out_3 ));  // open: en
  Register #(.width(1), .trigger("rising"), .Select("low")) register_8 (
    .D(RegWrite), .Q(RegWrite_2), .clk(in_10), .clr(\异步清零转同步清零_1_out_3 ));  // open: en
  \异步清零转同步清零  \u_异步清零转同步清零_1  (.clk(in_10), .clr(clr), .out_3(\异步清零转同步清零_1_out_3 ));
  Register #(.width(32), .trigger("rising"), .Select("low")) register_9 (
    .D(in_12), .Q(out_26), .clk(in_10), .clr(\异步清零转同步清零_1_out_3 ));  // open: en
  Register #(.width(32), .trigger("rising"), .Select("low")) register_10 (
    .D(B), .Q(out_27), .clk(in_10), .clr(\异步清零转同步清零_1_out_3 ));  // open: en
  Register #(.width(32), .trigger("rising"), .Select("low")) register_11 (
    .D(imm32), .Q(out_28), .clk(in_10), .clr(\异步清零转同步清零_1_out_3 ));  // open: en
  Register #(.width(5), .trigger("rising"), .Select("low")) register_12 (
    .D(rt), .Q(out_29), .clk(in_10), .clr(\异步清零转同步清零_1_out_3 ));  // open: en
  Register #(.width(5), .trigger("rising"), .Select("low")) register_13 (
    .D(rd), .Q(out_30), .clk(in_10), .clr(\异步清零转同步清零_1_out_3 ));  // open: en

  // Notes on the sheet:
  //   红色线是因为有的隐秘的地方连上了
  //   告诉我们：先单独调试好子电路，在综合调试
endmodule

module \异步清零转同步清零  (
  input  clk,
  input  clr,
  output out_3
);

  D_Flip_Flop #(.trigger("rising"), .Pre_Clr_Positions("ABOVE_BELOW"), .NegatePresetClear("false"), .enable("false"), .NewFFLayout("true")) d_ff_1 (
    .clk(clk), .D(clr), .Q(out_3));  // open: Qn, preset, reset
endmodule

module ALUcontrol (
  input  [3:0] ALUOp,
  input  [5:0] func,
  output [3:0] Op
);

  wire and_1_out, and_2_out, and_3_out, and_4_out, and_5_out, and_6_out, and_7_out, and_8_out, and_9_out,
       and_10_out, and_11_out, and_12_out, and_13_out, and_14_out, and_15_out, and_16_out, and_17_out,
       and_18_out, and_19_out, and_20_out, and_21_out, and_22_out, and_23_out, and_24_out, and_25_out,
       and_26_out, and_27_out, and_28_out, and_29_out, and_30_out, and_31_out, and_32_out, and_33_out,
       and_34_out, and_35_out, and_36_out, and_37_out, and_38_out, and_39_out, and_40_out, and_41_out,
       and_42_out, and_43_out, and_44_out, and_45_out, and_46_out, and_47_out, and_48_out, and_49_out,
       and_50_out, and_51_out, and_52_out, and_53_out, and_54_out, and_55_out, and_56_out, and_57_out,
       and_58_out, and_59_out, and_60_out, and_61_out, and_62_out, and_63_out, and_64_out, and_65_out,
       and_66_out, and_67_out, and_68_out, and_69_out, and_70_out, and_71_out, and_72_out, and_73_out,
       and_74_out, and_75_out, and_76_out, and_77_out, and_78_out, and_79_out, and_80_out, and_81_out,
       and_82_out, and_83_out, and_84_out, and_85_out, and_86_out, and_87_out, and_88_out, and_89_out,
       and_90_out, and_91_out, and_92_out, and_93_out, and_94_out, and_95_out, and_96_out, and_97_out,
       and_98_out, and_99_out, and_100_out, and_101_out, and_102_out, and_103_out, and_104_out, and_105_out,
       and_106_out, and_107_out, and_108_out, and_109_out, and_110_out, and_111_out, and_112_out,
       and_113_out, and_114_out, not_1_out, not_2_out, not_3_out, not_4_out, not_5_out, not_6_out, not_7_out,
       not_8_out, not_9_out, not_10_out, not_11_out, not_12_out, not_13_out, not_14_out, not_15_out,
       not_16_out, not_17_out, not_18_out, not_19_out, not_20_out, not_21_out, not_22_out, not_23_out,
       not_24_out, not_25_out, not_26_out, not_27_out, not_28_out, not_29_out, not_30_out, not_31_out,
       not_32_out, not_33_out, not_34_out, not_35_out, not_36_out, not_37_out, not_38_out, not_39_out,
       not_40_out, not_41_out, not_42_out, not_43_out, not_44_out, not_45_out, not_46_out, not_47_out,
       not_48_out, not_49_out, not_50_out, not_51_out, not_52_out, not_53_out, not_54_out, not_55_out,
       not_56_out, not_57_out, not_58_out, not_59_out, not_60_out, not_61_out, not_62_out, not_63_out,
       not_64_out, not_65_out, not_66_out, not_67_out, not_68_out, not_69_out, not_70_out, not_71_out,
       not_72_out, not_73_out, not_74_out, not_75_out, not_76_out, not_77_out, not_78_out, not_79_out,
       not_80_out, not_81_out, not_82_out, not_83_out, not_84_out, not_85_out, not_86_out, not_87_out,
       not_88_out, not_89_out, not_90_out, not_91_out, not_92_out, not_93_out, not_94_out, not_95_out,
       or_1_out, or_2_out, or_3_out, or_4_out, or_5_out, or_6_out, or_7_out, or_8_out, or_10_out, or_11_out,
       or_12_out, or_13_out;

  not not_1 (not_1_out, ALUOp[3]);
  not not_2 (not_2_out, ALUOp[2]);
  not not_3 (not_3_out, func[4]);
  not not_4 (not_4_out, func[3]);
  not not_5 (not_5_out, ALUOp[3]);
  not not_6 (not_6_out, ALUOp[2]);
  not not_7 (not_7_out, func[4]);
  not not_8 (not_8_out, func[3]);
  not not_9 (not_9_out, ALUOp[3]);
  not not_10 (not_10_out, func[4]);
  not not_11 (not_11_out, func[3]);
  not not_12 (not_12_out, ALUOp[3]);
  not not_13 (not_13_out, ALUOp[2]);
  not not_14 (not_14_out, func[4]);
  not not_15 (not_15_out, func[3]);
  not not_16 (not_16_out, ALUOp[3]);
  not not_17 (not_17_out, ALUOp[2]);
  not not_18 (not_18_out, func[4]);
  not not_19 (not_19_out, func[3]);
  not not_20 (not_20_out, ALUOp[3]);
  not not_21 (not_21_out, ALUOp[2]);
  not not_22 (not_22_out, func[4]);
  not not_23 (not_23_out, func[3]);
  not not_24 (not_24_out, ALUOp[3]);
  not not_25 (not_25_out, ALUOp[2]);
  not not_26 (not_26_out, func[4]);
  not not_27 (not_27_out, func[3]);
  not not_28 (not_28_out, ALUOp[3]);
  not not_29 (not_29_out, ALUOp[2]);
  not not_30 (not_30_out, func[4]);
  not not_31 (not_31_out, func[3]);
  and and_1 (and_1_out, not_1_out, not_2_out);
  not not_32 (not_32_out, ALUOp[1]);
  not not_33 (not_33_out, ALUOp[0]);
  not not_34 (not_34_out, func[5]);
  and and_2 (and_2_out, not_3_out, not_4_out);
  not not_35 (not_35_out, func[2]);
  not not_36 (not_36_out, func[1]);
  not not_37 (not_37_out, func[0]);
  and and_3 (and_3_out, not_5_out, not_6_out);
  not not_38 (not_38_out, ALUOp[1]);
  not not_39 (not_39_out, ALUOp[0]);
  not not_40 (not_40_out, func[5]);
  and and_4 (and_4_out, not_7_out, not_8_out);
  not not_41 (not_41_out, func[2]);
  not not_42 (not_42_out, func[0]);
  and and_5 (and_5_out, not_9_out, ALUOp[2]);
  not not_43 (not_43_out, func[5]);
  and and_6 (and_6_out, not_10_out, not_11_out);
  not not_44 (not_44_out, func[2]);
  not not_45 (not_45_out, func[0]);
  and and_7 (and_7_out, not_12_out, not_13_out);
  not not_46 (not_46_out, ALUOp[1]);
  not not_47 (not_47_out, ALUOp[0]);
  and and_8 (and_8_out, not_14_out, not_15_out);
  not not_48 (not_48_out, func[2]);
  not not_49 (not_49_out, func[1]);
  and and_9 (and_9_out, not_16_out, not_17_out);
  not not_50 (not_50_out, ALUOp[1]);
  not not_51 (not_51_out, ALUOp[0]);
  and and_10 (and_10_out, not_18_out, not_19_out);
  not not_52 (not_52_out, func[0]);
  not not_53 (not_53_out, ALUOp[3]);
  not not_54 (not_54_out, func[4]);
  not not_55 (not_55_out, func[3]);
  and and_11 (and_11_out, not_20_out, not_21_out);
  not not_56 (not_56_out, ALUOp[1]);
  not not_57 (not_57_out, ALUOp[0]);
  not not_58 (not_58_out, func[5]);
  and and_12 (and_12_out, not_22_out, not_23_out);
  not not_59 (not_59_out, func[2]);
  not not_60 (not_60_out, func[0]);
  and and_13 (and_13_out, not_24_out, not_25_out);
  not not_61 (not_61_out, ALUOp[1]);
  not not_62 (not_62_out, ALUOp[0]);
  and and_14 (and_14_out, not_26_out, not_27_out);
  not not_63 (not_63_out, func[2]);
  not not_64 (not_64_out, func[1]);
  and and_15 (and_15_out, not_28_out, not_29_out);
  not not_65 (not_65_out, ALUOp[1]);
  not not_66 (not_66_out, ALUOp[0]);
  and and_16 (and_16_out, not_30_out, not_31_out);
  not not_67 (not_67_out, func[1]);
  not not_68 (not_68_out, ALUOp[3]);
  not not_69 (not_69_out, func[4]);
  not not_70 (not_70_out, func[3]);
  and and_17 (and_17_out, and_1_out, not_32_out);
  and and_18 (and_18_out, and_17_out, and_19_out);
  and and_19 (and_19_out, not_33_out, not_34_out);
  and and_20 (and_20_out, and_2_out, not_35_out);
  and and_21 (and_21_out, and_20_out, and_22_out);
  and and_22 (and_22_out, not_36_out, not_37_out);
  and and_23 (and_23_out, and_3_out, not_38_out);
  and and_24 (and_24_out, and_23_out, and_25_out);
  and and_25 (and_25_out, not_39_out, not_40_out);
  and and_26 (and_26_out, and_4_out, not_41_out);
  and and_27 (and_27_out, and_26_out, and_28_out);
  and and_28 (and_28_out, func[1], not_42_out);
  not not_71 (not_71_out, ALUOp[3]);
  and and_29 (and_29_out, not_71_out, ALUOp[2]);
  not not_72 (not_72_out, ALUOp[1]);
  and and_30 (and_30_out, not_72_out, not_73_out);
  not not_73 (not_73_out, ALUOp[0]);
  and and_31 (and_31_out, and_5_out, ALUOp[1]);
  and and_32 (and_32_out, and_31_out, and_33_out);
  and and_33 (and_33_out, ALUOp[0], not_43_out);
  and and_34 (and_34_out, and_6_out, not_44_out);
  and and_35 (and_35_out, and_34_out, and_36_out);
  and and_36 (and_36_out, func[1], not_45_out);
  and and_37 (and_37_out, and_7_out, not_46_out);
  and and_38 (and_38_out, and_37_out, and_39_out);
  and and_39 (and_39_out, not_47_out, func[5]);
  and and_40 (and_40_out, and_8_out, not_48_out);
  and and_41 (and_41_out, and_40_out, and_42_out);
  and and_42 (and_42_out, not_49_out, func[0]);
  and and_43 (and_43_out, and_9_out, not_50_out);
  and and_44 (and_44_out, and_43_out, and_45_out);
  and and_45 (and_45_out, not_51_out, func[5]);
  and and_46 (and_46_out, and_10_out, func[2]);
  and and_47 (and_47_out, and_46_out, and_48_out);
  and and_48 (and_48_out, func[1], not_52_out);
  not not_74 (not_74_out, ALUOp[3]);
  and and_49 (and_49_out, not_74_out, not_75_out);
  not not_75 (not_75_out, ALUOp[2]);
  and and_50 (and_50_out, ALUOp[1], ALUOp[0]);
  not not_76 (not_76_out, ALUOp[3]);
  and and_51 (and_51_out, not_76_out, ALUOp[2]);
  not not_77 (not_77_out, ALUOp[1]);
  and and_52 (and_52_out, not_77_out, not_78_out);
  not not_78 (not_78_out, ALUOp[0]);
  not not_79 (not_79_out, ALUOp[3]);
  and and_53 (and_53_out, not_79_out, ALUOp[2]);
  not not_80 (not_80_out, ALUOp[1]);
  and and_54 (and_54_out, not_80_out, ALUOp[0]);
  not not_81 (not_81_out, ALUOp[3]);
  and and_55 (and_55_out, not_81_out, ALUOp[2]);
  and and_56 (and_56_out, ALUOp[1], not_82_out);
  not not_82 (not_82_out, ALUOp[0]);
  and and_57 (and_57_out, not_53_out, ALUOp[2]);
  and and_58 (and_58_out, and_57_out, ALUOp[1]);
  and and_59 (and_59_out, ALUOp[0], not_83_out);
  not not_83 (not_83_out, func[5]);
  and and_60 (and_60_out, not_54_out, not_55_out);
  and and_61 (and_61_out, and_60_out, not_84_out);
  not not_84 (not_84_out, func[2]);
  and and_62 (and_62_out, func[1], not_85_out);
  not not_85 (not_85_out, func[0]);
  and and_63 (and_63_out, and_11_out, not_56_out);
  and and_64 (and_64_out, and_63_out, and_65_out);
  and and_65 (and_65_out, not_57_out, not_58_out);
  and and_66 (and_66_out, and_12_out, not_59_out);
  and and_67 (and_67_out, and_66_out, and_68_out);
  and and_68 (and_68_out, func[1], not_60_out);
  and and_69 (and_69_out, and_13_out, not_61_out);
  and and_70 (and_70_out, and_69_out, and_71_out);
  and and_71 (and_71_out, not_62_out, func[5]);
  and and_72 (and_72_out, and_14_out, not_63_out);
  and and_73 (and_73_out, and_72_out, and_74_out);
  and and_74 (and_74_out, not_64_out, func[0]);
  and and_75 (and_75_out, and_15_out, not_65_out);
  and and_76 (and_76_out, and_75_out, and_77_out);
  and and_77 (and_77_out, not_66_out, func[5]);
  and and_78 (and_78_out, and_16_out, func[2]);
  and and_79 (and_79_out, and_78_out, and_80_out);
  and and_80 (and_80_out, not_67_out, func[0]);
  not not_86 (not_86_out, ALUOp[3]);
  and and_81 (and_81_out, not_86_out, not_87_out);
  not not_87 (not_87_out, ALUOp[2]);
  and and_82 (and_82_out, ALUOp[1], not_88_out);
  not not_88 (not_88_out, ALUOp[0]);
  not not_89 (not_89_out, ALUOp[3]);
  and and_83 (and_83_out, not_89_out, ALUOp[2]);
  not not_90 (not_90_out, ALUOp[1]);
  and and_84 (and_84_out, not_90_out, ALUOp[0]);
  not not_91 (not_91_out, ALUOp[3]);
  and and_85 (and_85_out, not_91_out, ALUOp[2]);
  and and_86 (and_86_out, ALUOp[1], not_92_out);
  not not_92 (not_92_out, ALUOp[0]);
  and and_87 (and_87_out, not_68_out, ALUOp[2]);
  and and_88 (and_88_out, and_87_out, ALUOp[1]);
  and and_89 (and_89_out, ALUOp[0], not_93_out);
  not not_93 (not_93_out, func[5]);
  and and_90 (and_90_out, not_69_out, not_70_out);
  and and_91 (and_91_out, and_90_out, not_94_out);
  not not_94 (not_94_out, func[2]);
  and and_92 (and_92_out, func[1], not_95_out);
  not not_95 (not_95_out, func[0]);
  and and_93 (and_93_out, and_18_out, and_21_out);
  and and_94 (and_94_out, and_24_out, and_27_out);
  and and_95 (and_95_out, and_29_out, and_30_out);
  and and_96 (and_96_out, and_32_out, and_35_out);
  and and_97 (and_97_out, and_38_out, and_41_out);
  and and_98 (and_98_out, and_44_out, and_47_out);
  and and_99 (and_99_out, and_49_out, and_50_out);
  and and_100 (and_100_out, and_51_out, and_52_out);
  and and_101 (and_101_out, and_53_out, and_54_out);
  and and_102 (and_102_out, and_55_out, and_56_out);
  and and_103 (and_103_out, and_58_out, and_59_out);
  and and_104 (and_104_out, and_61_out, and_62_out);
  and and_105 (and_105_out, and_64_out, and_67_out);
  and and_106 (and_106_out, and_70_out, and_73_out);
  and and_107 (and_107_out, and_76_out, and_79_out);
  and and_108 (and_108_out, and_81_out, and_82_out);
  and and_109 (and_109_out, and_83_out, and_84_out);
  and and_110 (and_110_out, and_85_out, and_86_out);
  and and_111 (and_111_out, and_88_out, and_89_out);
  and and_112 (and_112_out, and_91_out, and_92_out);
  or or_1 (or_1_out, and_93_out, and_94_out);
  or or_2 (or_2_out, and_95_out, and_96_out);
  or or_3 (or_3_out, and_97_out, and_98_out);
  or or_4 (or_4_out, and_99_out, and_100_out);
  or or_5 (or_5_out, and_101_out, and_102_out);
  and and_113 (and_113_out, and_103_out, and_104_out);
  or or_6 (or_6_out, and_105_out, and_106_out);
  or or_7 (or_7_out, and_107_out, and_108_out);
  or or_8 (or_8_out, and_109_out, and_110_out);
  and and_114 (and_114_out, and_111_out, and_112_out);
  or or_9 (Op[2], or_1_out, or_2_out);
  or or_10 (or_10_out, or_3_out, or_4_out);
  or or_11 (or_11_out, or_5_out, and_113_out);
  or or_12 (or_12_out, or_6_out, or_7_out);
  or or_13 (or_13_out, or_8_out, and_114_out);
  or or_14 (Op[1], or_10_out, or_11_out);
  or or_15 (Op[0], or_12_out, or_13_out);

  assign Op[3] = 1'b0;
endmodule
